// Logisim project carry_save_adder.circ as structural Verilog: 1 circuit, main circuit CSA
module CSA (
  input  x,
  input  y,
  input  R,
  input  clk,
  output pp
);

  wire adder_1_cout, adder_1_out, and_1_out, d_ff_2_q, xor_1_out, xor_2_out;

  xor xor_1 (xor_1_out, x, adder_1_out);
  and and_1 (and_1_out, x, adder_1_out);
  D_Flip_Flop d_ff_1 (.D(xor_1_out), .clk(clk), .Q(pp), .preset(1'b0), .reset(R));  // open: Qn
  Adder #(.width(1)) adder_1 (.a(y), .b(d_ff_2_q), .out(adder_1_out), .cin(1'b0), .cout(adder_1_cout));
  D_Flip_Flop d_ff_2 (.D(xor_2_out), .clk(clk), .Q(d_ff_2_q), .preset(1'b0), .reset(R));  // open: Qn
  xor xor_2 (xor_2_out, and_1_out, adder_1_cout);

  // Notes on the sheet:
  //   X
  //   Y
  //   R
  //   Sum
endmodule
